// Logisim project exp 33.circ as structural Verilog: 1 circuit, main circuit main
module main (
  input  in_1,
  input  in_2,
  input  in_3,
  output out_4,
  output out_5
);

  wire and_1_out, xor_1_out;

  xor xor_1 (xor_1_out, in_1, in_2);
  and and_1 (and_1_out, in_1, in_2);
  xor xor_2 (out_4, xor_1_out, in_3);
  // AND_Gate and_2 has open pins: in0=xor_1_out, in1=in_3, out=open
  buf or_1 (out_5, and_1_out);  // OR_Gate
endmodule
